# Fritzing sketch kegwasher (saved by Fritzing 1.0.4)
breadboards: 4

parts:
  Composant1 = Arduino Uno (Rev3) - ICSP
  Display1 = LCD screen 16x2 HD44780
  S2 = Adafruit 3104 lighted pushbutton [package=THT]
  J1 = Piezo Speaker
  RY1 = SSR-40VA
  U1 = 16-Channel Relay Module [package=relay-16ch]
  VALVE_SANITIZER_IN = Plastic Solenoid Valve
  WATER_PUMP1 = water pump/motor
  LCM1602_IIC1 = LCM1602 IIC [part_number="LCM1602 IIC" chip_label="LCM1602 IIC" package="DIP (Dual Inline) [THT]"]
  PID_CR20 = PID CR20 CANARD ROUGE [package=2x5-ra]
  M1 = pt100
  VALVE_AIR = Plastic Solenoid Valve small
  VALVE_CO2 = Plastic Solenoid Valve small
  VALVE_CLEANER_IN = Plastic Solenoid Valve
  VALVE5 = Plastic Solenoid Valve
  VALVE_CLEANER_OUT = Plastic Solenoid Valve
  VALVE_SANITIZER_OUT = Plastic Solenoid Valve
  VALVE_DRAIN = Plastic Solenoid Valve
  D5 = Diode [package=diode-hv]  # not connected
  D6 = Diode [package=diode-hv]  # not connected
  D9 = Diode [package=diode-hv]  # not connected
  A2 = Immersion Heater
  Power_plug_220v1 = Power plug 220v
  A3 = CHINT-NCH8-2020
  S6 = Round Pushbutton
  J3 = 220v plug
  HLK-PM2 = HLK-PM12 [part_number=HLK-PM12]
  D10 = Diode [package=diode-hv]  # not connected
  D11 = Diode [package=diode-hv]  # not connected
  D12 = Diode [package=diode-hv]  # not connected
  D13 = Diode [package=diode-hv]  # not connected
  D14 = Diode [package=diode-hv]  # not connected
  D15 = Diode [package=diode-hv]  # not connected
  D16 = Diode [package=diode-hv]  # not connected
  D17 = Diode [package=diode-hv]  # not connected
  D18 = Diode [package=diode-hv]  # not connected
  D19 = Diode [package=diode-hv]  # not connected
  D20 = Diode [package=diode-hv]  # not connected
  D21 = Diode [package=diode-hv]  # not connected
  D22 = Diode [package=diode-hv]  # not connected
  Power_plug_220v2 = Power plug 220v
  Power_plug_220v3 = Power plug 220v
  J4 = 220v plug
  J6 = 220v plug
  ENCODER = Rotary Encoder with Knob
  R1 = Resistor [tolerance=±5% resistance=220 package="0402 [SMD]"]

nets:
  N1: Composant1.A1, ENCODER.OUT_A
  N2: Composant1.A2, ENCODER.OUT_B
  N3: Composant1.A3, ENCODER.SW
  N4: Composant1.A4/SDA, LCM1602_IIC1.SDA
  N5: Composant1.A5/SCL, LCM1602_IIC1.SCL
  N6: Composant1.D8, U1.IN10
  N7: Composant1.D9_PWM, U1.IN9
  N8: Composant1.D10_PWM/SS, U1.IN1
  N9: Composant1.D11_PWM/MOSI, R1.Pin_1
  N10: Composant1.D2, U1.IN16
  N11: Composant1.D3_PWM, U1.IN15
  N12: Composant1.D4, U1.IN14
  N13: Composant1.D5_PWM, U1.IN13
  N14: Composant1.D6_PWM, U1.IN12
  N15: Composant1.D7, U1.IN11
  GND: Composant1.GND, S2.pin_5, J1.pin1, U1.GND, U1.OUT_GND, VALVE_SANITIZER_IN.no_name_yet#1, LCM1602_IIC1.GND, VALVE_AIR.no_name_yet#1, VALVE_CO2.no_name_yet#1, VALVE_CLEANER_IN.no_name_yet#1, VALVE5.no_name_yet#1, VALVE_CLEANER_OUT.no_name_yet#1, VALVE_SANITIZER_OUT.no_name_yet#1, VALVE_DRAIN.no_name_yet#1, HLK-PM2.-Vo, ENCODER.GND_1, ENCODER.GND_2
  N16: Composant1.VIN, U1.VCCOUT_5V
  VSS: Display1.VSS, LCM1602_IIC1.VSS
  VDD: Display1.VDD, LCM1602_IIC1.VDD
  N17: Display1.VO, LCM1602_IIC1.V0
  N18: Display1.RS, LCM1602_IIC1.RS
  N19: Display1.R_W, LCM1602_IIC1.RW
  N20: Display1.E, LCM1602_IIC1.E
  N21: Display1.DB0, LCM1602_IIC1.D0
  N22: Display1.DB1, LCM1602_IIC1.D1
  N23: Display1.DB2, LCM1602_IIC1.D2
  N24: Display1.DB3, LCM1602_IIC1.D3
  N25: Display1.DB4, LCM1602_IIC1.D4
  N26: Display1.DB5, LCM1602_IIC1.D5
  N27: Display1.DB6, LCM1602_IIC1.D6
  N28: Display1.DB7, LCM1602_IIC1.D7
  N29: Display1.A, LCM1602_IIC1.A
  N30: Display1.K, LCM1602_IIC1.K
  N31: S2.pin_6, R1.Pin_0
  N32: RY1.Pin_1, RY1.Pin_2, U1.K1_NO, U1.K1_COM, PID_CR20.1, Power_plug_220v1.P, Power_plug_220v1.E, A3.Pin_1, J3.E, HLK-PM2.AC_1, Power_plug_220v2.P, Power_plug_220v2.E, Power_plug_220v3.P, Power_plug_220v3.E
  N33: RY1.Pin_3, PID_CR20.3
  N34: RY1.Pin_4, PID_CR20.4
  N35: U1.VCC, U1.K9_COM, U1.K10_COM, U1.K11_COM, U1.K12_COM, U1.K13_COM, U1.K14_COM, U1.K15_COM, U1.K16_COM, HLK-PM2.+Vo
  N36: U1.K9_NO, VALVE_DRAIN.no_name_yet#2
  N37: U1.K10_NO, VALVE_SANITIZER_OUT.no_name_yet#2
  N38: U1.K11_NO, VALVE_CLEANER_OUT.no_name_yet#2
  N39: U1.K12_NO, VALVE_SANITIZER_IN.no_name_yet#2
  N40: U1.K13_NO, VALVE_CLEANER_IN.no_name_yet#2
  N41: U1.K14_NO, VALVE5.no_name_yet#2
  N42: U1.K15_NO, VALVE_CO2.no_name_yet#2
  N43: U1.K16_NO, VALVE_AIR.no_name_yet#2
  N44: WATER_PUMP1.pin_1, J6.N
  N45: WATER_PUMP1.pin_2, J6.P
  N46: LCM1602_IIC1.LED_A, LCM1602_IIC1.LED_B
  N47: PID_CR20.2, Power_plug_220v1.N, A3.Pin_3, J3.N, HLK-PM2.AC_2, Power_plug_220v2.N, Power_plug_220v3.N
  N48: PID_CR20.8, M1.pin3
  N49: PID_CR20.9, PID_CR20.10, M1.pin1, M1.pin2
  N50: A2.P, J4.P
  N51: A2.N, J4.N
  N52: A2.E, J4.E
  N53: A3.Pin_4, S6.leg0
  N54: A3.Pin_6, S6.leg1, J3.P

custom parts:
  LCD screen 16x2 HD44780: LCD screen with HD44780 controller enables showing text, symbols, value or anything else that comes from Croduino/Arduino. It is capable of showing 16 symbols in two lines and therefore can be used in many projects that need to send clearly visible and legible output information.. • Color of symbols: White • Backlight: Blue • Dimensions: 80 x 36 x 12 mm • Screen dimensions: 64.5 x 16 mm •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
  Adafruit 3104 lighted pushbutton: This Mini Illuminated Momentary Power Button it an adorable breadboard-friendly tactile switch that has a built-in LED. It provides a simple way to add a tactile switch and a colorful universal power symbol to your project.
  SSR-40VA: SSR-40VA solid state relay.
  16-Channel Relay Module: 16 channel relay module
  water pump/motor: WATER PUMP BY ARDUBLOCKTR
  LCM1602 IIC: I2C-Module to use a 1602 or 2004 LCD on with the wire.h libory Serial LCD Modul
  PID CR20 CANARD ROUGE: PID temperature controller commonly used for brewing beer
  pt100: CrocSee RTD Pt100 Temperature Sensor Probe 3 Wires 2M Cable Thermocouple -58~572°F (-50-300°C) 1/2" BSP Thread.
  Immersion Heater: Immersion Heater 220V with eart protection
  Power plug 220v: power plug 220v with earth protection
  CHINT-NCH8-2020: CHINT NCH8-20A 25A 40A 63A Modular AC household Mini Contactor 220V 230V 400V 1NO 1NC 2NO 2NC.
  Round Pushbutton: A generic pushbutton.
  220v plug: Generic 220V AC plug with earth connection
  HLK-PM12: AC-DC 220V to 12V Step-Down Power Supply Module forked from Iyad Nahas
  Rotary Encoder with Knob: Rotary Encoder with 1/4" Shaft and Knob
